# Fritzing sketch OctoAlarmWiring (saved by Fritzing 1.0.1rc)
breadboards: 1

parts:
  Part1 = Arduino Nano (Rev3.0)
  J1 = Piezo Speaker
  Part2 = LED Tactile Button Breakout v10 [part_number=BOB-10467]
  Part4 = NRF24L01

nets:
  GND: Part1.GND, J1.pin1, Part2.1, Part2.4, Part4.GND
  N1: Part1.D3, J1.pin2
  N2: Part1.D6, Part2.2
  N3: Part1.D9, Part4.CE
  N4: Part1.D10, Part4.CSN
  N5: Part1.D11/MOSI, Part4.MOSI
  N6: Part1.D12/MISO, Part4.MISO
  3V3: Part1.3V3, Part4.VCC
  N7: Part1.D13/SCK, Part4.SCK

notes:
  Version 1.2
