# Fritzing sketch OctoRemoteWiring (saved by Fritzing 1.0.1rc)
breadboards: 1

parts:
  Part5 = Arduino Nano (Rev3.0)
  Part6 = LED Tactile Button Breakout v10 [part_number=BOB-10467]
  Part7 = NRF24L01

nets:
  GND: Part5.GND, Part6.1, Part6.4, Part7.GND
  N1: Part5.D6, Part6.2
  N2: Part5.D7, Part6.3
  N3: Part5.D9, Part7.CE
  N4: Part5.D10, Part7.CSN
  N5: Part5.D11/MOSI, Part7.MOSI
  N6: Part5.D12/MISO, Part7.MISO
  3V3: Part5.3V3, Part7.VCC
  N7: Part5.D13/SCK, Part7.SCK

notes:
  Version 0.2
